// Logisim project 74151多路选择器实现函数.circ as structural Verilog: 2 circuits, main circuit 74151
module _74151 (
  input  D0,
  input  D1,
  input  D2,
  input  D3,
  input  D4,
  input  D5,
  input  D6,
  input  D7,
  input  A,
  input  B,
  input  D,
  output W,
  output Y
);

  wire and_1_out, and_2_out, and_3_out, and_4_out, and_5_out, and_6_out, and_7_out, and_8_out, not_1_out,
       not_2_out, not_3_out, not_4_out, not_5_out, not_6_out, not_7_out;

  not not_1 (not_1_out, A);
  not not_2 (not_2_out, B);
  not not_3 (not_3_out, D);
  not not_4 (not_4_out, not_1_out);
  not not_5 (not_5_out, not_2_out);
  not not_6 (not_6_out, not_3_out);
  not not_7 (not_7_out, 1'b0);
  and and_1 (and_1_out, not_7_out, not_1_out, not_3_out, not_2_out, D0);
  and and_2 (and_2_out, not_7_out, not_1_out, not_6_out, not_2_out, D1);
  and and_3 (and_3_out, not_7_out, not_1_out, not_3_out, not_5_out, D2);
  and and_4 (and_4_out, not_7_out, not_1_out, not_6_out, not_5_out, D3);
  and and_5 (and_5_out, not_7_out, not_4_out, not_3_out, not_2_out, D4);
  and and_6 (and_6_out, not_7_out, not_4_out, not_6_out, not_2_out, D5);
  and and_7 (and_7_out, not_7_out, not_4_out, not_3_out, not_5_out, D6);
  and and_8 (and_8_out, not_7_out, not_4_out, not_6_out, not_5_out, D7);
  nor nor_1 (W, and_1_out, and_2_out, and_3_out, and_4_out, and_5_out, and_6_out, and_7_out, and_8_out);
  not not_8 (Y, W);
endmodule

module Function (
  input  A,
  input  B,
  input  C,
  input  D,
  input  E,
  output out_6
);

  wire n74151_1_y, n74151_2_y, n74151_3_y, n74151_4_y, not_1_out;

  not not_1 (not_1_out, 1'b0);
  _74151 u_74151_1 (
    .D0(1'b0), .D1(not_1_out), .D2(not_1_out), .D3(not_1_out), .D4(not_1_out), .D5(1'b0), .D6(1'b0),
    .D7(not_1_out), .A(C), .B(B), .D(A), .Y(n74151_1_y));  // open: W
  _74151 u_74151_2 (
    .D0(not_1_out), .D1(1'b0), .D2(not_1_out), .D3(1'b0), .D4(1'b0), .D5(not_1_out), .D6(not_1_out),
    .D7(1'b0), .A(C), .B(B), .D(A), .Y(n74151_2_y));  // open: W
  _74151 u_74151_3 (
    .D0(1'b0), .D1(not_1_out), .D2(1'b0), .D3(not_1_out), .D4(not_1_out), .D5(not_1_out), .D6(1'b0),
    .D7(not_1_out), .A(C), .B(B), .D(A), .Y(n74151_3_y));  // open: W
  _74151 u_74151_4 (
    .D0(not_1_out), .D1(1'b0), .D2(not_1_out), .D3(1'b0), .D4(not_1_out), .D5(1'b0), .D6(not_1_out),
    .D7(not_1_out), .A(C), .B(B), .D(A), .Y(n74151_4_y));  // open: W
  _74151 u_74151_5 (
    .D0(n74151_1_y), .D1(n74151_2_y), .D2(n74151_3_y), .D3(n74151_4_y), .D4(1'b0), .D5(1'b0), .D6(1'b0),
    .D7(1'b0), .A(1'b0), .B(E), .D(D), .Y(out_6));  // open: W
endmodule
