// Logisim project exam2.circ as structural Verilog: 7 circuits, main circuit main
module main (
  input  in_1,
  output [2:0] out_2
);

  wire clock_1_out, next0, next1, next2, state0, state1, state2;

  Clock clock_1 (.out(clock_1_out));
  D_Flip_Flop d_ff_1 (.clk(clock_1_out), .D(next0), .Q(state0));  // open: Qn, preset, en, reset
  D_Flip_Flop d_ff_2 (.clk(clock_1_out), .D(next1), .Q(state1));  // open: Qn, preset, en, reset
  D_Flip_Flop d_ff_3 (.clk(clock_1_out), .D(next2), .Q(state2));  // open: Qn, preset, en, reset
  transNext0 transnext0_1 (.state0(state0), .state1(state1), .state2(state2), .\input (in_1), .next0(next0));
  transNext1 transnext1_1 (.state0(state0), .state1(state1), .state2(state2), .\input (in_1), .next1(next1));
  transNext2 transnext2_1 (.state0(state0), .state1(state1), .state2(state2), .\input (in_1), .next2(next2));
  transOut0 transout0_1 (.state0(state0), .state1(state1), .state2(state2), .output0(out_2[0]));
  transOut1 transout1_1 (.state0(state0), .state1(state1), .state2(state2), .output1(out_2[1]));
  transOut2 transout2_1 (.state0(state0), .state1(state1), .state2(state2), .output2(out_2[2]));

  // Other names for the same wires on the sheet: input = in_1; output0 = out_2[0]; output1 = out_2[1];
  //   output2 = out_2[2]
endmodule

module transNext0 (
  input  state0,
  input  state1,
  input  state2,
  input  \input ,
  output next0
);

  wire and_1_out, and_2_out, not_1_out, not_2_out, not_3_out, not_4_out;

  not not_1 (not_1_out, state2);
  not not_2 (not_2_out, state1);
  not not_3 (not_3_out, state2);
  not not_4 (not_4_out, state0);
  and and_1 (and_1_out, not_1_out, not_2_out, state0, \input );
  or or_1 (next0, and_1_out, and_2_out);
  and and_2 (and_2_out, not_3_out, state1, not_4_out);
endmodule

module transNext1 (
  input  state0,
  input  state1,
  input  state2,
  input  \input ,
  output next1
);

  wire not_1_out, not_2_out;

  not not_1 (not_1_out, state2);
  not not_2 (not_2_out, state1);
  and and_1 (next1, not_1_out, not_2_out, \input );
endmodule

module transNext2 (
  input  state0,
  input  state1,
  input  state2,
  input  \input ,
  output next2
);

  wire not_1_out, not_2_out;

  not not_1 (not_1_out, state2);
  not not_2 (not_2_out, state1);
  and and_1 (next2, not_1_out, not_2_out, state0, \input );
endmodule

module transOut0 (
  input  state0,
  input  state1,
  input  state2,
  output output0
);

  wire and_1_out, and_2_out, not_1_out, not_2_out;

  not not_1 (not_1_out, state2);
  not not_2 (not_2_out, state1);
  and and_1 (and_1_out, not_1_out, not_2_out, state0);
  and and_2 (and_2_out, state2, state1, state0);
  or or_1 (output0, and_1_out, and_2_out);
endmodule

module transOut1 (
  input  state0,
  input  state1,
  input  state2,
  output output1
);

  wire not_1_out, not_2_out;

  not not_1 (not_1_out, state2);
  not not_2 (not_2_out, state0);
  and and_1 (output1, not_1_out, state1, not_2_out);
endmodule

module transOut2 (
  input  state0,
  input  state1,
  input  state2,
  output output2
);

  wire not_1_out, not_2_out, not_3_out;

  not not_1 (not_1_out, state2);
  not not_2 (not_2_out, state1);
  not not_3 (not_3_out, state0);
  and and_1 (output2, not_1_out, not_2_out, not_3_out);
endmodule
