// Logisim project test2.circ as structural Verilog: 1 circuit, main circuit test2
module test2 (
  input  [31:0] A,
  input  [31:0] B,
  input  [31:0] C,
  output [31:0] R
);

  wire [31:0] adder_1_out;

  Adder #(.width(32)) adder_1 (.a(A), .b(B), .out(adder_1_out));  // open: cin, cout
  Subtractor #(.width(32)) subtractor_1 (.a(adder_1_out), .b(C), .out(R));  // open: bin, bout
endmodule
