// Logisim project test3.circ as structural Verilog: 1 circuit, main circuit test3
module test3 (
  input  [7:0] A,
  input  [7:0] B,
  input  [7:0] C,
  input  [7:0] D,
  input  [1:0] Sel,
  output [7:0] R
);

  Multiplexer #(.select(2), .width(8)) multiplexer_1 (
    .in0(A), .in1(B), .in2(C), .in3(D), .out(R), .sel(Sel));  // open: en
endmodule
