// Logisim project 三进制半加器&全加器.circ as structural Verilog: 2 circuits, main circuit 三进制半加器
module \三进制半加器  (
  input  [1:0] in_1,
  input  [1:0] in_2,
  output Carry,
  output [1:0] s1s0
);

  wire a0___b0_out, a0___b1_out, a0_nb0_nb1_out, a1___b0_out, a1___b1_out, a1_nb0_nb1_out, na0_na1_out,
       na0_na1b0_out, na0_na1b1_out, nb0_nb1_out, not_1_out, not_2_out, not_3_out, not_4_out;

  not not_1 (not_1_out, in_1[0]);
  not not_2 (not_2_out, in_1[1]);
  not not_3 (not_3_out, in_2[0]);
  not not_4 (not_4_out, in_2[1]);
  and a1___b1 (a1___b1_out, in_1[1], in_2[1]);
  and a1___b0 (a1___b0_out, in_1[1], in_2[0]);
  and a0___b1 (a0___b1_out, in_1[0], in_2[1]);
  and a0___b0 (a0___b0_out, in_1[0], in_2[0]);
  and na0_na1 (na0_na1_out, not_1_out, not_2_out);
  and nb0_nb1 (nb0_nb1_out, not_3_out, not_4_out);
  and na0_na1b1 (na0_na1b1_out, na0_na1_out, in_2[1]);
  and a1_nb0_nb1 (a1_nb0_nb1_out, in_1[1], nb0_nb1_out);
  or or_1 (Carry, a1___b1_out, a1___b0_out, a0___b1_out);
  or or_2 (s1s0[1], na0_na1b1_out, a1_nb0_nb1_out, a0___b0_out);
  and na0_na1b0 (na0_na1b0_out, na0_na1_out, in_2[0]);
  and a0_nb0_nb1 (a0_nb0_nb1_out, nb0_nb1_out, in_1[0]);
  or or_3 (s1s0[0], na0_na1b0_out, a0_nb0_nb1_out, a1___b1_out);
endmodule

module \三进制全加器  (
  input  [1:0] A,
  input  [1:0] B,
  input  Cin,
  output Carry,
  output [1:0] Sum
);

  wire \三进制半加器_1_carry , \三进制半加器_2_carry ;
  wire [1:0] \三进制半加器_1_s1s0 ;

  \三进制半加器  \u_三进制半加器_1  (.in_1(A), .in_2(B), .Carry(\三进制半加器_1_carry ), .s1s0(\三进制半加器_1_s1s0 ));
  \三进制半加器  \u_三进制半加器_2  (.in_1(\三进制半加器_1_s1s0 ), .in_2({1'b0, Cin}), .Carry(\三进制半加器_2_carry ), .s1s0(Sum));
  or or_1 (Carry, \三进制半加器_1_carry , \三进制半加器_2_carry );
endmodule
