// Logisim project exam3.circ as structural Verilog: 1 circuit, main circuit sold
module sold (
  input  [2:0] in_1,
  output out_2,
  output [1:0] out_3
);

  wire and_2_out, and_3_out, and_4_out, and_5_out, and_6_out, and_7_out, and_8_out, and_9_out, and_10_out,
       and_11_out, and_12_out, and_13_out, clock_1_out, nand_1_out, Next0, Next1, Next2, not_1_out,
       not_2_out, not_3_out, not_4_out, not_5_out, not_6_out, not_7_out, not_8_out, not_9_out, not_10_out,
       not_11_out, or_2_out, or_6_out, State0, State1, State2, xor_1_out;

  Clock clock_1 (.out(clock_1_out));
  D_Flip_Flop d_ff_1 (.clk(clock_1_out), .D(Next0), .Q(State0));  // open: Qn, preset, en, reset
  D_Flip_Flop d_ff_2 (.clk(clock_1_out), .D(Next1), .Q(State1));  // open: Qn, preset, en, reset
  D_Flip_Flop d_ff_3 (.clk(clock_1_out), .D(Next2), .Q(State2));  // open: Qn, preset, en, reset
  not not_1 (not_1_out, State2);
  nand nand_1 (nand_1_out, State1, in_1[1]);
  xor xor_1 (xor_1_out, State0, in_1[0]);
  not not_2 (not_2_out, in_1[2]);
  and and_1 (Next0, not_1_out, nand_1_out, not_2_out, xor_1_out);
  not not_3 (not_3_out, State2);
  not not_4 (not_4_out, State0);
  not not_5 (not_5_out, State1);
  not not_6 (not_6_out, in_1[2]);
  and and_2 (and_2_out, not_4_out, not_3_out, in_1[1], not_5_out);
  and and_3 (and_3_out, not_4_out, in_1[0], not_3_out, State1);
  and and_4 (and_4_out, State0, not_6_out, not_3_out, not_5_out);
  or or_1 (Next1, and_2_out, and_3_out, and_4_out);
  or or_2 (or_2_out, State0, State1);
  and and_5 (and_5_out, State0, State1);
  not not_7 (not_7_out, in_1[0]);
  and and_6 (and_6_out, in_1[2], or_2_out);
  and and_7 (and_7_out, and_5_out, not_7_out);
  not not_8 (not_8_out, State0);
  not not_9 (not_9_out, State1);
  not not_10 (not_10_out, State2);
  or or_3 (out_2, State2, and_6_out, and_7_out);
  and and_8 (and_8_out, not_10_out, not_9_out, not_8_out, in_1[2]);
  and and_9 (and_9_out, not_10_out, State1, not_8_out, in_1[1]);
  and and_10 (and_10_out, not_10_out, State1, State0, in_1[0]);
  or or_4 (Next2, and_8_out, and_9_out, and_10_out);
  not not_11 (not_11_out, State0);
  and and_11 (and_11_out, State2, ~in_1[0]);  // AND_Gate
  and and_12 (and_12_out, State0, State1);
  and and_13 (and_13_out, not_11_out, State1, in_1[2]);
  or or_5 (out_3[0], and_13_out, and_11_out);
  and and_14 (out_3[1], in_1[2], or_6_out);
  or or_6 (or_6_out, State2, and_12_out);

  // Other names for the same wires on the sheet: Input0 = in_1[0]; Input1 = in_1[1]; Input2 = in_1[2];
  //   Charge0 = out_3[0]; Charge1 = out_3[1]; Sell = out_2
endmodule
