// Logisim project test3.circ as structural Verilog: 1 circuit, main circuit xmod5
module xmod5 (
  input  in_1,
  output [2:0] out_2
);

  wire and_1_out, and_2_out, and_3_out, and_4_out, and_5_out, and_6_out, and_7_out, clock_1_out, Next0,
       Next1, Next2, nor_1_out, not_1_out, xor_1_out, xor_2_out, xor_3_out, xor_4_out, xor_5_out;

  Clock clock_1 (.out(clock_1_out));
  xor xor_1 (xor_1_out, out_2[0], out_2[2]);
  xor xor_2 (xor_2_out, out_2[1], out_2[2]);
  D_Flip_Flop d_ff_1 (.clk(clock_1_out), .D(Next0), .Q(out_2[0]));  // open: Qn, preset, en, reset
  D_Flip_Flop d_ff_2 (.clk(clock_1_out), .D(Next1), .Q(out_2[1]));  // open: Qn, preset, en, reset
  D_Flip_Flop d_ff_3 (.clk(clock_1_out), .D(Next2), .Q(out_2[2]));  // open: Qn, preset, en, reset
  nor nor_1 (nor_1_out, out_2[1], out_2[2]);
  and and_1 (and_1_out, xor_1_out, xor_2_out);
  not not_1 (not_1_out, in_1);
  and and_2 (and_2_out, nor_1_out, in_1);
  and and_3 (and_3_out, and_1_out, not_1_out);
  or or_1 (Next0, and_2_out, and_3_out);
  and and_4 (and_4_out, out_2[0], ~out_2[1], ~out_2[2]);  // AND_Gate
  xor xor_3 (xor_3_out, out_2[2], out_2[0]);
  xor xor_4 (xor_4_out, out_2[2], out_2[1]);
  xor xor_5 (xor_5_out, out_2[2], in_1);
  and and_5 (and_5_out, xor_3_out, xor_4_out, xor_5_out);
  or or_2 (Next1, and_4_out, and_5_out);
  and and_6 (and_6_out, ~out_2[0], ~out_2[1], out_2[2], in_1);  // AND_Gate
  and and_7 (and_7_out, ~out_2[0], out_2[1], ~out_2[2], ~in_1);  // AND_Gate
  or or_3 (Next2, and_6_out, and_7_out);

  // Other names for the same wires on the sheet: Input = in_1; State0 = out_2[0]; State1 = out_2[1];
  //   State2 = out_2[2]
endmodule
