// Logisim project test4.circ as structural Verilog: 1 circuit, main circuit password
module password (
  input  in_1,
  input  in_2,
  input  in_3,
  input  in_4,
  input  in_5,
  output [3:0] out_6
);

  wire and_1_out, and_2_out, and_3_out, and_4_out, and_5_out, and_6_out, and_7_out, and_8_out, and_9_out,
       not_1_out, not_2_out, not_3_out, not_4_out, not_5_out, not_6_out, or_2_out, or_3_out;

  not not_1 (not_1_out, in_5);
  not not_2 (not_2_out, not_1_out);
  not not_3 (not_3_out, not_1_out);
  not not_4 (not_4_out, in_5);
  not not_5 (not_5_out, in_5);
  and and_1 (and_1_out, in_2, not_1_out);
  and and_2 (and_2_out, in_1, not_2_out);
  and and_3 (and_3_out, in_2, not_3_out);
  and and_4 (and_4_out, in_1, not_1_out);
  and and_5 (and_5_out, in_4, in_5);
  and and_6 (and_6_out, in_3, not_4_out);
  and and_7 (and_7_out, in_4, not_5_out);
  and and_8 (and_8_out, in_3, in_5);
  or or_1 (out_6[3], and_1_out, and_2_out);
  or or_2 (or_2_out, and_3_out, and_4_out);
  or or_3 (or_3_out, and_5_out, and_6_out);
  or or_4 (out_6[0], and_7_out, and_8_out);
  and and_9 (and_9_out, or_2_out, or_3_out);
  not not_6 (not_6_out, and_9_out);
  and and_10 (out_6[2], or_2_out, not_6_out);
  and and_11 (out_6[1], not_6_out, or_3_out);
endmodule
