// Logisim project exam2.circ as structural Verilog: 2 circuits, main circuit FSM
module FSM (
  input  [1:0] in_1,
  output out_2
);

  wire clock_1_out;
  wire [1:0] register_1_q, transfer_1_out_3;

  transfer transfer_1 (.state(register_1_q), .\input (in_1), .out_3(transfer_1_out_3));
  Clock clock_1 (.out(clock_1_out));
  Register #(.width(2)) register_1 (.D(transfer_1_out_3), .Q(register_1_q), .clk(clock_1_out));  // open: en, clr
  and and_1 (out_2, register_1_q[0], register_1_q[1]);
endmodule

module transfer (
  input  [1:0] state,
  input  [1:0] \input ,
  output [1:0] out_3
);

  wire and_1_out, and_2_out, and_3_out, and_4_out, and_5_out, not_1_out, not_2_out, not_3_out, not_4_out;

  not not_1 (not_1_out, state[1]);
  not not_2 (not_2_out, \input [0]);
  not not_3 (not_3_out, state[0]);
  not not_4 (not_4_out, \input [1]);
  and and_1 (and_1_out, not_1_out, state[0], \input [1], not_2_out);
  and and_2 (and_2_out, state[1], not_3_out, \input [1]);
  and and_3 (and_3_out, state[1], \input [1], \input [0]);
  and and_4 (and_4_out, not_4_out, \input [0]);
  or or_1 (out_3[0], and_4_out, and_5_out);
  and and_5 (and_5_out, state[1], \input [0]);
  or or_2 (out_3[1], and_1_out, and_2_out, and_3_out);
endmodule
