// Logisim project test1.circ as structural Verilog: 1 circuit, main circuit voter
module voter (
  input  s1,
  input  s2,
  input  s3,
  input  ss,
  output O
);

  wire and_1_out, and_2_out, and_3_out;

  and and_1 (and_1_out, s2, s3, ss);
  and and_2 (and_2_out, s1, s3, ss);
  and and_3 (and_3_out, s1, s2, ss);
  or or_1 (O, and_1_out, and_2_out, and_3_out);
endmodule
