// Logisim project test2.circ as structural Verilog: 1 circuit, main circuit responder
module responder (
  input  s1,
  input  s2,
  input  s3,
  input  ss,
  output [2:0] out_5
);

  wire and_1_out, and_2_out, and_3_out, clock_1_out, d_ff_4_q, nor_1_out, not_1_out;

  Clock clock_1 (.out(clock_1_out));
  and and_1 (and_1_out, nor_1_out, s1);
  and and_2 (and_2_out, nor_1_out, s2);
  and and_3 (and_3_out, nor_1_out, s3);
  not not_1 (not_1_out, ss);
  D_Flip_Flop d_ff_1 (.clk(and_1_out), .D(d_ff_4_q), .Q(out_5[2]), .reset(not_1_out));  // open: Qn, preset, en
  D_Flip_Flop d_ff_2 (.clk(and_2_out), .D(d_ff_4_q), .Q(out_5[1]), .reset(not_1_out));  // open: Qn, preset, en
  D_Flip_Flop d_ff_3 (.clk(and_3_out), .D(d_ff_4_q), .Q(out_5[0]), .reset(not_1_out));  // open: Qn, preset, en
  D_Flip_Flop d_ff_4 (.clk(clock_1_out), .D(ss), .Q(d_ff_4_q));  // open: Qn, preset, en, reset
  nor nor_1 (nor_1_out, out_5[2], out_5[1], out_5[0]);
endmodule
