// Logisim project test3.circ as structural Verilog: 3 circuits, main circuit 2nmod5
module _2nmod5 (
  input  in_1,
  output [2:0] out_2
);

  wire clock_1_out;
  wire [1:0] register_1_q, transfer_1_out_3;

  transfer transfer_1 (.in_1(in_1), .in_2(register_1_q), .out_3(transfer_1_out_3));
  Clock clock_1 (.out(clock_1_out));
  Register #(.width(2)) register_1 (.D(transfer_1_out_3), .Q(register_1_q), .clk(clock_1_out));  // open: en, clr
  \output  output_1 (.in_1(register_1_q), .in_2(in_1), .out_3(out_2));
endmodule

module transfer (
  input  in_1,
  input  [1:0] in_2,
  output [1:0] out_3
);


  assign out_3 = {in_2[0], in_1};
endmodule

module \output  (
  input  [1:0] in_1,
  input  in_2,
  output [2:0] out_3
);

  wire and_1_out, and_2_out, not_1_out, not_2_out;

  not not_1 (not_1_out, in_2);
  not not_2 (not_2_out, in_1[0]);
  and and_1 (and_1_out, in_1[0], in_2);
  and and_2 (and_2_out, not_2_out, not_1_out);
  or or_1 (out_3[0], and_1_out, and_2_out);
  and and_3 (out_3[2], in_1[0], not_1_out);

  assign out_3[1] = in_2;
endmodule
