// Logisim project cpu.circ as structural Verilog
module main (
  input  in_1,
  output [31:0] pc,
  output [31:0] inst,
  output reg_write,
  output [4:0] reg_addr,
  output [31:0] reg_data_in,
  output mem_write,
  output [9:0] mem_addr,
  output \正常停机 ,
  output \无法解析的指令 ,
  output \除0异常 ,
  output halt,
  output \步数超出限制 ,
  output [31:0] count
);

  wire alu_1_equal, \b跳转判断_1_b跳转 , clock_1_out, clock_2_out, clock_3_out, clock_4_out, \control_1__4字节访存 ,
       \control_1_alu源操作数 , control_1_beq, control_1_bgez, control_1_bne, \control_1_hilo写入 , control_1_j,
       control_1_jr, control_1_lbu, ext, not_1_out, not_2_out, \读内存 ;
  wire [1:0] \control_1_hilo读取 , \control_1_目标寄存器 ;
  wire [2:0] priority_encoder_1_out;
  wire [3:0] control_1_alu_op;
  wire [4:0] \寄存器地址生成_1_rs , \寄存器地址生成_1_rt ;
  wire [9:0] \右移2位再取低10位_1_out_2 ;
  wire [31:0] adder_1_out, \alu操作数1 , \alu操作数2 , \alu运算结果 , HI, \hi_lo_寄存器_1_hi , \hi_lo_寄存器_1_lo ,
       \load处理_1_访存结果 , multiplexer_1_out, ram_1_data, \RAM写入内容 , reg_file_1_rd1, reg_file_1_rd2,
       \地址计算_1_b指令跳转地址 , \地址计算_1_j_jal跳转地址 , \地址计算_1_无跳转地址 , \立即数处理_1__32位立即数 , \运算_访存综合结果 ;

  Comparator #(.width(32)) comparator_1 (.a(32'h1000), .b(count), .lt(\步数超出限制 ));  // open: gt, eq
  not not_1 (not_1_out, halt);
  Counter #(.width(32), .max('hffffffff)) counter_1 (
    .count(not_1_out), .Q(count), .clk(clock_1_out));  // open: load, D, carry, clr, preset, down
  Clock clock_1 (.out(clock_1_out));
  // Probe on count
  or or_1 (halt, \无法解析的指令 , \正常停机 , \除0异常 , \步数超出限制 );
  // Probe on multiplexer_1_out
  Multiplexer #(.select(3), .width(32), .enable("false")) multiplexer_1 (
    .in0(\地址计算_1_无跳转地址 ), .in1(\地址计算_1_b指令跳转地址 ), .in2(\地址计算_1_j_jal跳转地址 ), .in3(\alu操作数1 ), .in4(32'h3000),
    .out(multiplexer_1_out), .sel(priority_encoder_1_out));  // open: in5, in6, in7
  Register #(.width(32), .Select("low")) register_1 (
    .D(multiplexer_1_out), .en(not_2_out), .Q(pc), .clk(clock_2_out));  // open: clr
  Clock clock_2 (.out(clock_2_out));
  not not_2 (not_2_out, halt);
  // Probe on pc
  // Mips_Probe mips_probe_1: pin names not known; wires that end beside it: inst
  Priority_Encoder priority_encoder_1 (
    .in0(1'b1), .in1(\b跳转判断_1_b跳转 ), .in2(control_1_j), .in3(control_1_jr), .in4(in_1),
    .out(priority_encoder_1_out));  // open: in5, in6, in7, gs, en_out, en_in
  \地址计算  \u_地址计算_1  (
    .\指令 (inst), .pc(pc), .\B指令跳转地址 (\地址计算_1_b指令跳转地址 ), .\J_Jal跳转地址 (\地址计算_1_j_jal跳转地址 ),
    .\无跳转地址 (\地址计算_1_无跳转地址 ));
  \右移2位再取低10位  \u_右移2位再取低10位_1  (.in_1(pc), .out_2(\右移2位再取低10位_1_out_2 ));
  LED led_1 (.in(\正常停机 ));
  LED led_2 (.in(\无法解析的指令 ));
  LED led_3 (.in(\除0异常 ));
  // Probe on reg_data_in
  Adder #(.width(32)) adder_1 (.a(pc), .b(32'h4), .out(adder_1_out));  // open: cin, cout
  \虚假寄存器堆  \u_虚假寄存器堆_1  ();
  LED led_4 (.in(reg_write));
  // Mips_Probe mips_probe_2: pin names not known; wires that end beside it: inst
  ROM #(.addrWidth(10), .dataWidth(32), .Select("high")) rom_1 (.addr(\右移2位再取低10位_1_out_2 ), .data(inst));
  LED led_5 (.in(\步数超出限制 ));
  // Probe on \alu操作数1 
  \虚假alu  \u_虚假alu_1  ();
  // Probe on \alu操作数2 
  \寄存器地址生成  \u_寄存器地址生成_1  (
    .\指令 (inst), .rs(\寄存器地址生成_1_rs ), .rt(\寄存器地址生成_1_rt ), .\写入地址 (reg_addr), .\寄存器写入地址选择 (\control_1_目标寄存器 ));
  // Probe on \alu运算结果 
  // Probe on HI
  control control_1 (
    .\指令 (inst), .\寄存器写使能 (reg_write), .\目标寄存器 (\control_1_目标寄存器 ), .\立即数符号扩展 (ext),
    .\alu源操作数 (\control_1_alu源操作数 ), .\读内存 (\读内存 ), .\写内存 (mem_write), .beq(control_1_beq), .j(control_1_j),
    .alu_op(control_1_alu_op), .jr(control_1_jr), .bne(control_1_bne), .\_4字节访存 (\control_1__4字节访存 ),
    .lbu(control_1_lbu), .bgez(control_1_bgez), .stop(\正常停机 ), .\hilo写入 (\control_1_hilo写入 ),
    .\hilo读取 (\control_1_hilo读取 ), .\指令无法解析 (\无法解析的指令 ));
  Multiplexer #(.width(32), .enable("false")) multiplexer_2 (
    .in0(\运算_访存综合结果 ), .in1(adder_1_out), .out(reg_data_in), .sel(\control_1_目标寄存器 [1]));
  \b跳转判断  \b跳转判断_1  (
    .\b跳转 (\b跳转判断_1_b跳转 ), .beq(control_1_beq), .bne(control_1_bne), .equal(alu_1_equal),
    .bgez(control_1_bgez), .\寄存器值 (\alu操作数1 ));
  \hi_lo_寄存器  \hi_lo_寄存器_1  (
    .\HI输入 (HI), .\LO输入 (\alu运算结果 ), .HI(\hi_lo_寄存器_1_hi ), .LO(\hi_lo_寄存器_1_lo ), .clk(clock_3_out),
    .reset(in_1), .we(\control_1_hilo写入 ));
  Clock clock_3 (.out(clock_3_out));
  reg_file reg_file_1 (
    .A1(\寄存器地址生成_1_rs ), .A2(\寄存器地址生成_1_rt ), .A3(reg_addr), .WD(reg_data_in), .RD1(reg_file_1_rd1),
    .RD2(reg_file_1_rd2), .clk(clock_3_out), .reset(in_1), .we(reg_write));
  LED led_6 (.in(mem_write));
  \立即数处理  \u_立即数处理_1  (.\_16位立即数 (inst[15:0]), .\_32位立即数 (\立即数处理_1__32位立即数 ), .\符号扩展 (ext));
  \虚假RAM  \u_虚假ram_1  ();
  // Probe on mem_addr
  // Probe on \RAM写入内容 
  Multiplexer #(.select(2), .width(32), .enable("false")) multiplexer_3 (
    .in0(\hi_lo_寄存器_1_hi ), .in1(\hi_lo_寄存器_1_lo ), .in2(reg_file_1_rd1), .in3(reg_file_1_rd1),
    .out(\alu操作数1 ), .sel(\control_1_hilo读取 ));
  Multiplexer #(.width(32), .enable("false")) multiplexer_4 (
    .in0(\立即数处理_1__32位立即数 ), .in1(reg_file_1_rd2), .out(\alu操作数2 ), .sel(\control_1_alu源操作数 ));
  alu alu_1 (
    .in_1(\alu操作数1 ), .in_2(\alu操作数2 ), .in_3(control_1_alu_op), .equal(alu_1_equal), .out_5(\alu运算结果 ),
    .HI(HI), ._0(\除0异常 ));
  LED led_7 (.in(\读内存 ));
  // Probe on \运算_访存综合结果 
  \右移2位再取低10位  \u_右移2位再取低10位_2  (.in_1(\alu运算结果 ), .out_2(mem_addr));
  \store处理  \store处理_1  (
    .\目前此内存地址的数据 (ram_1_data), .\准备写入的数据 (reg_file_1_rd2), .\实际写入的数据 (\RAM写入内容 ), .\完整内存地址 (\alu运算结果 ),
    .\_4字节访存 (\control_1__4字节访存 ));
  Clock clock_4 (.out(clock_4_out));
  RAM #(.addrWidth(10), .dataWidth(32), .bus("separate"), .simpleMode("false"), .Select("low")) ram_1 (
    .addr(mem_addr), .din(\RAM写入内容 ), .data(ram_1_data), .str(mem_write), .clk(clock_4_out), .ld(\读内存 ),
    .clr(in_1));  // open: sel
  \load处理  \load处理_1  (
    .\内存读出内容 (ram_1_data), .\访存结果 (\load处理_1_访存结果 ), .\完整内存地址 (\alu运算结果 ), .lbu(control_1_lbu),
    .\_4字节访存 (\control_1__4字节访存 ));
  Multiplexer #(.width(32), .enable("false")) multiplexer_5 (
    .in0(\alu运算结果 ), .in1(\load处理_1_访存结果 ), .out(\运算_访存综合结果 ), .sel(\读内存 ));

  // Other names for the same wires on the sheet: _0 = \除0异常 ; reset = in_1; stop = halt; 写内存 = mem_write;
  //   写寄存器 = reg_write; 寄存器写入内容[31:0] = reg_data_in; 寄存器写入地址[4:0] = reg_addr; 指令[31:0] = inst; 访存地址[9:0] = mem_addr

  // Notes on the sheet:
  //   jr：寄存器跳转
  //   无跳转：pc+4
  //   b系列指令：pc+4+imm16
  //   j、jal：{pc[31:28], imm26, 2'b00}
  //   pc
  //   取指
  //   访问寄存器
  //   j、jal
  //   jr
  //   指令rom
  //   b
  //   pc+4
  //   运算
  //   访存
  //   运算结果
endmodule

module control (
  input  [31:0] \指令 ,
  output stop,
  output \寄存器写使能 ,
  output [1:0] \目标寄存器 ,
  output \立即数符号扩展 ,
  output \alu源操作数 ,
  output lbu,
  output \读内存 ,
  output \写内存 ,
  output bgez,
  output bne,
  output beq,
  output j,
  output jr,
  output [1:0] \hilo读取 ,
  output \hilo写入 ,
  output \_4字节访存 ,
  output [3:0] alu_op,
  output \指令无法解析 
);

  wire add, addiu, addu, \and , comparator_13_eq, comparator_15_eq, comparator_16_eq, comparator_17_eq,
       comparator_18_eq, comparator_19_eq, comparator_20_eq, comparator_21_eq, comparator_22_eq,
       comparator_23_eq, comparator_24_eq, comparator_25_eq, comparator_26_eq, comparator_27_eq,
       comparator_28_eq, comparator_29_eq, comparator_30_eq, comparator_31_eq, divu, j_t, jal, lb, lui, lw,
       mfhi, mflo, mul, multu, \or , or_1_out, or_2_out, or_3_out, or_4_out, or_5_out, or_12_out, or_16_out,
       ori, R_type, sb, sll, slt, sltu, sub, subu, sw;

  Comparator #(.width(6), .mode("unsigned")) comparator_1 (.a(\指令 [31:26]), .b(6'b001101), .eq(ori));  // open: gt, lt
  Comparator #(.width(6), .mode("unsigned")) comparator_2 (.a(\指令 [31:26]), .b(6'b100011), .eq(lw));  // open: gt, lt
  Comparator #(.width(6), .mode("unsigned")) comparator_3 (.a(\指令 [31:26]), .b(6'b101011), .eq(sw));  // open: gt, lt
  Comparator #(.width(6), .mode("unsigned")) comparator_4 (.a(\指令 [31:26]), .b(6'b000100), .eq(beq));  // open: gt, lt
  Comparator #(.width(6), .mode("unsigned")) comparator_5 (.a(\指令 [31:26]), .b(6'b000010), .eq(j_t));  // open: gt, lt
  Comparator #(.width(6), .mode("unsigned")) comparator_6 (.a(\指令 [31:26]), .b(6'b000011), .eq(jal));  // open: gt, lt
  Comparator #(.width(6), .mode("unsigned")) comparator_7 (.a(\指令 [31:26]), .b(6'b001001), .eq(addiu));  // open: gt, lt
  Comparator #(.width(6), .mode("unsigned")) comparator_8 (.a(\指令 [31:26]), .b(6'b001111), .eq(lui));  // open: gt, lt
  Comparator #(.width(6), .mode("unsigned")) comparator_9 (.a(\指令 [31:26]), .b(6'b100000), .eq(lb));  // open: gt, lt
  Comparator #(.width(6), .mode("unsigned")) comparator_10 (.a(\指令 [31:26]), .b(6'b100100), .eq(lbu));  // open: gt, lt
  or or_1 (or_1_out, multu, mul);
  or or_2 (or_2_out, addu, \读内存 , \写内存 , addiu, add);
  or or_3 (or_3_out, sub, subu);
  or or_4 (or_4_out, ori, \or );
  or or_5 (or_5_out, mfhi, mflo);
  Comparator #(.width(6), .mode("unsigned")) comparator_11 (.a(\指令 [31:26]), .b(6'b101000), .eq(sb));  // open: gt, lt
  Comparator #(.width(6), .mode("unsigned")) comparator_12 (.a(\指令 [31:26]), .b(6'b000101), .eq(bne));  // open: gt, lt
  Comparator #(.width(6), .mode("unsigned")) comparator_13 (
    .a(\指令 [31:26]), .b(6'b011100), .eq(comparator_13_eq));  // open: gt, lt
  Comparator #(.width(6), .mode("unsigned")) comparator_14 (.a(\指令 [31:26]), .b(6'b000001), .eq(bgez));  // open: gt, lt
  assign alu_op = sll ? 4'b0000 : 4'bz;  // Controlled_Buffer controlled_buffer_1
  assign alu_op = or_1_out ? 4'b0011 : 4'bz;  // Controlled_Buffer controlled_buffer_2
  assign alu_op = divu ? 4'b0100 : 4'bz;  // Controlled_Buffer controlled_buffer_3
  assign alu_op = or_2_out ? 4'b0101 : 4'bz;  // Controlled_Buffer controlled_buffer_4
  assign alu_op = or_3_out ? 4'b0110 : 4'bz;  // Controlled_Buffer controlled_buffer_5
  assign alu_op = \and  ? 4'b0111 : 4'bz;  // Controlled_Buffer controlled_buffer_6
  assign alu_op = or_4_out ? 4'b1000 : 4'bz;  // Controlled_Buffer controlled_buffer_7
  assign alu_op = slt ? 4'b1011 : 4'bz;  // Controlled_Buffer controlled_buffer_8
  assign alu_op = sltu ? 4'b1100 : 4'bz;  // Controlled_Buffer controlled_buffer_9
  assign alu_op = or_5_out ? 4'b1101 : 4'bz;  // Controlled_Buffer controlled_buffer_10
  assign alu_op = lui ? 4'b1111 : 4'bz;  // Controlled_Buffer controlled_buffer_11
  Comparator #(.width(6), .mode("unsigned")) comparator_15 (
    .a(\指令 [5:0]), .b(6'b000010), .eq(comparator_15_eq));  // open: gt, lt
  or or_6 (\读内存 , lw, lb, lbu);
  or or_7 (\写内存 , sw, sb);
  or or_8 (\_4字节访存 , lw, sw);
  and and_1 (mul, comparator_15_eq, comparator_13_eq);
  Pull_Resistor pull_resistor_1 (.node(alu_op));
  Comparator #(.width(6), .mode("unsigned")) comparator_16 (
    .a(\指令 [31:26]), .b({6{1'b0}}), .eq(comparator_16_eq));  // open: gt, lt
  // Probe on \指令 [5:0]
  Comparator #(.width(6), .mode("unsigned")) comparator_17 (
    .a(\指令 [5:0]), .b(6'b100000), .eq(comparator_17_eq));  // open: gt, lt
  Comparator #(.width(6), .mode("unsigned")) comparator_18 (
    .a(\指令 [5:0]), .b(6'b100001), .eq(comparator_18_eq));  // open: gt, lt
  Comparator #(.width(6), .mode("unsigned")) comparator_19 (
    .a(\指令 [5:0]), .b(6'b100010), .eq(comparator_19_eq));  // open: gt, lt
  Comparator #(.width(6), .mode("unsigned")) comparator_20 (
    .a(\指令 [5:0]), .b(6'b100011), .eq(comparator_20_eq));  // open: gt, lt
  Comparator #(.width(6), .mode("unsigned")) comparator_21 (
    .a(\指令 [5:0]), .b(6'b001000), .eq(comparator_21_eq));  // open: gt, lt
  Comparator #(.width(6), .mode("unsigned")) comparator_22 (
    .a(\指令 [5:0]), .b(6'b101010), .eq(comparator_22_eq));  // open: gt, lt
  Comparator #(.width(6), .mode("unsigned")) comparator_23 (
    .a(\指令 [5:0]), .b(6'b101011), .eq(comparator_23_eq));  // open: gt, lt
  Comparator #(.width(6), .mode("unsigned")) comparator_24 (
    .a(\指令 [5:0]), .b({6{1'b0}}), .eq(comparator_24_eq));  // open: gt, lt
  Comparator #(.width(6), .mode("unsigned")) comparator_25 (
    .a(\指令 [5:0]), .b(6'b100100), .eq(comparator_25_eq));  // open: gt, lt
  Comparator #(.width(6), .mode("unsigned")) comparator_26 (
    .a(\指令 [5:0]), .b(6'b100101), .eq(comparator_26_eq));  // open: gt, lt
  Comparator #(.width(6), .mode("unsigned")) comparator_27 (
    .a(\指令 [5:0]), .b(6'b001100), .eq(comparator_27_eq));  // open: gt, lt
  Comparator #(.width(6), .mode("unsigned")) comparator_28 (
    .a(\指令 [5:0]), .b(6'b011001), .eq(comparator_28_eq));  // open: gt, lt
  Comparator #(.width(6), .mode("unsigned")) comparator_29 (
    .a(\指令 [5:0]), .b(6'b011011), .eq(comparator_29_eq));  // open: gt, lt
  Comparator #(.width(6), .mode("unsigned")) comparator_30 (
    .a(\指令 [5:0]), .b(6'b010000), .eq(comparator_30_eq));  // open: gt, lt
  Comparator #(.width(6), .mode("unsigned")) comparator_31 (
    .a(\指令 [5:0]), .b(6'b010010), .eq(comparator_31_eq));  // open: gt, lt
  or or_9 (R_type, add, addu, subu, slt, \or , sltu, sll, \and , mul);
  and and_2 (add, comparator_16_eq, comparator_17_eq);
  and and_3 (addu, comparator_16_eq, comparator_18_eq);
  and and_4 (sub, comparator_16_eq, comparator_19_eq);
  and and_5 (subu, comparator_16_eq, comparator_20_eq);
  and and_6 (jr, comparator_16_eq, comparator_21_eq);
  and and_7 (slt, comparator_16_eq, comparator_22_eq);
  and and_8 (sltu, comparator_16_eq, comparator_23_eq);
  and and_9 (sll, comparator_16_eq, comparator_24_eq);
  and and_10 (\and , comparator_16_eq, comparator_25_eq);
  and and_11 (\or , comparator_16_eq, comparator_26_eq);
  and and_12 (stop, comparator_16_eq, comparator_27_eq);
  and and_13 (multu, comparator_16_eq, comparator_28_eq);
  and and_14 (divu, comparator_16_eq, comparator_29_eq);
  and and_15 (mfhi, comparator_16_eq, comparator_30_eq);
  and and_16 (mflo, comparator_16_eq, comparator_31_eq);
  or or_10 (\hilo写入 , multu, divu);
  or or_11 (\寄存器写使能 , lui, addiu, R_type, ori, \读内存 , jal, mflo, mfhi);
  not not_1 (\指令无法解析 , or_12_out);
  or or_12 (or_12_out, ori, beq, j_t, jal, addiu, lui, stop, bne, bgez, multu, divu, mfhi, mflo, jr, \读内存 , \写内存 , R_type);
  buf or_13 (\目标寄存器 [1], jal);  // OR_Gate
  or or_14 (\目标寄存器 [0], R_type, mflo, mfhi);
  or or_15 (\立即数符号扩展 , \读内存 , \写内存 , beq, bne, addiu);
  or or_16 (or_16_out, ori, \读内存 , \写内存 , addiu, lui);
  not not_2 (\alu源操作数 , or_16_out);
  or or_17 (j, jal, j_t);
  assign \hilo读取  = mflo ? 2'b01 : 2'bz;  // Controlled_Buffer controlled_buffer_12
  Pull_Resistor #(.pull(1)) pull_resistor_2 (.node(\hilo读取 ));
  assign \hilo读取  = mfhi ? 2'b00 : 2'bz;  // Controlled_Buffer controlled_buffer_13

  // Other names for the same wires on the sheet: load = \读内存 ; store = \写内存 ; syscall = stop

  // Notes on the sheet:
  //   op func => 指令
  //   注：严谨来说，此处应判断rt字段是否为00001，从而区分bgez和bltz
  //   special
  //   需要写入reg的才算r type
  //   0写入rt
  //   1写入rd
  //   2写入$31
  //   3写入LO、HI
  //   0无符号扩展
  //   1有符号扩展
  //   指令 => 控制信号
  //   0使用立即数
  //   1使用寄存器值
  //   0读hi
  //   1读lo
  //   3不读hilo
endmodule

module alu (
  input  [31:0] in_1,
  input  [31:0] in_2,
  input  [3:0] in_3,
  output equal,
  output [31:0] out_5,
  output [31:0] HI,
  output _0
);

  wire comparator_2_lt, comparator_3_lt, comparator_4_eq, comparator_5_eq;
  wire [4:0] bit_extender_1_out;
  wire [31:0] adder_1_out, and_1_out, bit_extender_2_out, bit_extender_3_out, divider_1_out, divider_1_rem,
       divider_2_out, divider_2_rem, multiplier_1_cout, multiplier_1_out, multiplier_2_cout,
       multiplier_2_out, nor_1_out, or_1_out, shifter_1_out, shifter_2_out, shifter_3_out, shifter_4_out,
       subtractor_1_out, xor_1_out;

  Bit_Extender #(.in_width(32), .out_width(5), .\type ("zero")) bit_extender_1 (.in(in_2), .out(bit_extender_1_out));
  Comparator #(.width(32)) comparator_1 (.a(in_1), .b(in_2), .eq(equal));  // open: gt, lt
  Shifter #(.width(32)) shifter_1 (.in(in_1), .\dist (bit_extender_1_out), .out(shifter_1_out));
  Shifter #(.width(32), .shift("lr")) shifter_2 (.in(in_1), .\dist (bit_extender_1_out), .out(shifter_2_out));
  Shifter #(.width(32), .shift("ar")) shifter_3 (.in(in_1), .\dist (bit_extender_1_out), .out(shifter_3_out));
  Multiplier #(.width(32)) multiplier_1 (
    .a(in_1), .b(in_2), .out(multiplier_1_out), .cout(multiplier_1_cout));  // open: cin
  Divider #(.width(32)) divider_1 (.a(in_1), .b(in_2), .out(divider_1_out), .rem(divider_1_rem));  // open: upper
  Adder #(.width(32)) adder_1 (.a(in_1), .b(in_2), .out(adder_1_out));  // open: cin, cout
  Subtractor #(.width(32)) subtractor_1 (.a(in_1), .b(in_2), .out(subtractor_1_out));  // open: bin, bout
  assign and_1_out = in_1 & in_2;  // AND_Gate and_1, 32 bits wide
  assign or_1_out = in_1 | in_2;  // OR_Gate or_1, 32 bits wide
  assign xor_1_out = in_1 ^ in_2;  // XOR_Gate xor_1, 32 bits wide
  assign nor_1_out = ~(in_1 | in_2);  // NOR_Gate nor_1, 32 bits wide
  Comparator #(.width(32)) comparator_2 (.a(in_1), .b(in_2), .lt(comparator_2_lt));  // open: gt, eq
  Comparator #(.width(32), .mode("unsigned")) comparator_3 (.a(in_1), .b(in_2), .lt(comparator_3_lt));  // open: gt, eq
  Shifter #(.width(32)) shifter_4 (.in(in_2), .\dist (5'b10000), .out(shifter_4_out));
  assign bit_extender_2_out = {{31{1'b0}}, comparator_2_lt};  // Bit_Extender bit_extender_2
  assign bit_extender_3_out = {{31{1'b0}}, comparator_3_lt};  // Bit_Extender bit_extender_3
  Comparator #(.width(32)) comparator_4 (.a({32{1'b0}}), .b(in_2), .eq(comparator_4_eq));  // open: gt, lt
  Multiplexer #(.select(4), .width(32)) multiplexer_1 (
    .in0(shifter_1_out), .in1(shifter_2_out), .in2(shifter_3_out), .in3(multiplier_1_out),
    .in4(divider_1_out), .in5(adder_1_out), .in6(subtractor_1_out), .in7(and_1_out), .in8(or_1_out),
    .in9(xor_1_out), .in10(nor_1_out), .in11(bit_extender_2_out), .in12(bit_extender_3_out), .in13(in_1),
    .in15(shifter_4_out), .out(out_5), .sel(in_3));  // open: in14, en
  Multiplexer #(.select(4), .width(32)) multiplexer_2 (
    .in0({32{1'b0}}), .in1({32{1'b0}}), .in2({32{1'b0}}), .in3(multiplier_1_cout), .in4(divider_1_rem),
    .in5({32{1'b0}}), .in6({32{1'b0}}), .in7({32{1'b0}}), .in8({32{1'b0}}), .in9({32{1'b0}}),
    .in10({32{1'b0}}), .in11({32{1'b0}}), .in12({32{1'b0}}), .in13({32{1'b0}}), .in14({32{1'b0}}),
    .in15({32{1'b0}}), .out(HI), .sel(in_3));  // open: en
  Comparator #(.width(4)) comparator_5 (.a(in_3), .b(4'b0100), .eq(comparator_5_eq));  // open: gt, lt
  and and_2 (_0, comparator_5_eq, comparator_4_eq);
  // Probe on {32{1'b1}}
  // Probe on 32'h2
  // Probe on multiplier_2_out
  Multiplier #(.width(32)) multiplier_2 (
    .a({32{1'b1}}), .b(32'h2), .out(multiplier_2_out), .cout(multiplier_2_cout));  // open: cin
  // Probe on multiplier_2_cout
  // Probe on {32{1'b1}}
  // Probe on 32'h1
  Divider #(.width(32)) divider_2 (.a({32{1'b1}}), .b(32'h1), .out(divider_2_out), .rem(divider_2_rem));  // open: upper
  // Probe on divider_2_out
  // Probe on divider_2_rem

  // Other names for the same wires on the sheet: i1[31:0] = in_1; i2[31:0] = in_2; op[3:0] = in_3
endmodule

module reg_file (
  input  [4:0] A1,
  input  clk,
  input  reset,
  input  we,
  input  [4:0] A2,
  input  [4:0] A3,
  input  [31:0] WD,
  output [31:0] RD1,
  output [31:0] RD2
);

  wire [31:0] I0, I1, I2, I3, I4, I5, I6, I7, I8, I9, I10, I11, I12, I13, I14, I15, I16, I17, I18, I19, I20,
       I21, I22, I23, I24, I25, I26, I27, I28, I29, I30, I31, O0, O1, O2, O3, O4, O5, O6, O7, O8, O9, O10,
       O11, O12, O13, O14, O15, O16, O17, O18, O19, O20, O21, O22, O23, O24, O25, O26, O27, O28, O29, O30,
       O31;

  Demultiplexer #(.select(5), .width(32), .tristate("true")) demultiplexer_1 (
    .out0(I0), .out1(I1), .out2(I2), .out3(I3), .out4(I4), .out5(I5), .out6(I6), .out7(I7), .out8(I8),
    .out9(I9), .out10(I10), .out11(I11), .out12(I12), .out13(I13), .out14(I14), .out15(I15), .out16(I16),
    .out17(I17), .out18(I18), .out19(I19), .out20(I20), .out21(I21), .out22(I22), .out23(I23), .out24(I24),
    .out25(I25), .out26(I26), .out27(I27), .out28(I28), .out29(I29), .out30(I30), .out31(I31), .in(WD),
    .sel(A3));  // open: en
  Multiplexer #(.select(5), .width(32)) multiplexer_1 (
    .in0(O0), .in1(O1), .in2(O2), .in3(O3), .in4(O4), .in5(O5), .in6(O6), .in7(O7), .in8(O8), .in9(O9),
    .in10(O10), .in11(O11), .in12(O12), .in13(O13), .in14(O14), .in15(O15), .in16(O16), .in17(O17),
    .in18(O18), .in19(O19), .in20(O20), .in21(O21), .in22(O22), .in23(O23), .in24(O24), .in25(O25),
    .in26(O26), .in27(O27), .in28(O28), .in29(O29), .in30(O30), .in31(O31), .out(RD2), .sel(A2));  // open: en
  Multiplexer #(.select(5), .width(32)) multiplexer_2 (
    .in0(O0), .in1(O1), .in2(O2), .in3(O3), .in4(O4), .in5(O5), .in6(O6), .in7(O7), .in8(O8), .in9(O9),
    .in10(O10), .in11(O11), .in12(O12), .in13(O13), .in14(O14), .in15(O15), .in16(O16), .in17(O17),
    .in18(O18), .in19(O19), .in20(O20), .in21(O21), .in22(O22), .in23(O23), .in24(O24), .in25(O25),
    .in26(O26), .in27(O27), .in28(O28), .in29(O29), .in30(O30), .in31(O31), .out(RD1), .sel(A1));  // open: en
  Register #(.width(32), .Select("low")) register_1 (.D({32{1'b0}}), .en(we), .Q(O0), .clk(clk), .clr(reset));
  Register #(.width(32), .Select("low")) register_2 (.D(I8), .en(we), .Q(O8), .clk(clk), .clr(reset));
  Register #(.width(32), .Select("low")) register_3 (.D(I16), .en(we), .Q(O16), .clk(clk), .clr(reset));
  Register #(.width(32), .Select("low")) register_4 (.D(I24), .en(we), .Q(O24), .clk(clk), .clr(reset));
  Register #(.width(32), .Select("low")) register_5 (.D(I1), .en(we), .Q(O1), .clk(clk), .clr(reset));
  Register #(.width(32), .Select("low")) register_6 (.D(I9), .en(we), .Q(O9), .clk(clk), .clr(reset));
  Register #(.width(32), .Select("low")) register_7 (.D(I17), .en(we), .Q(O17), .clk(clk), .clr(reset));
  Register #(.width(32), .Select("low")) register_8 (.D(I25), .en(we), .Q(O25), .clk(clk), .clr(reset));
  Register #(.width(32), .Select("low")) register_9 (.D(I2), .en(we), .Q(O2), .clk(clk), .clr(reset));
  Register #(.width(32), .Select("low")) register_10 (.D(I10), .en(we), .Q(O10), .clk(clk), .clr(reset));
  Register #(.width(32), .Select("low")) register_11 (.D(I18), .en(we), .Q(O18), .clk(clk), .clr(reset));
  Register #(.width(32), .Select("low")) register_12 (.D(I26), .en(we), .Q(O26), .clk(clk), .clr(reset));
  Register #(.width(32), .Select("low")) register_13 (.D(I3), .en(we), .Q(O3), .clk(clk), .clr(reset));
  Register #(.width(32), .Select("low")) register_14 (.D(I11), .en(we), .Q(O11), .clk(clk), .clr(reset));
  Register #(.width(32), .Select("low")) register_15 (.D(I19), .en(we), .Q(O19), .clk(clk), .clr(reset));
  Register #(.width(32), .Select("low")) register_16 (.D(I27), .en(we), .Q(O27), .clk(clk), .clr(reset));
  Register #(.width(32), .Select("low")) register_17 (.D(I4), .en(we), .Q(O4), .clk(clk), .clr(reset));
  Register #(.width(32), .Select("low")) register_18 (.D(I12), .en(we), .Q(O12), .clk(clk), .clr(reset));
  Register #(.width(32), .Select("low")) register_19 (.D(I20), .en(we), .Q(O20), .clk(clk), .clr(reset));
  Register #(.width(32), .Select("low")) register_20 (.D(I28), .en(we), .Q(O28), .clk(clk), .clr(reset));
  Register #(.width(32), .Select("low")) register_21 (.D(I5), .en(we), .Q(O5), .clk(clk), .clr(reset));
  Register #(.width(32), .Select("low")) register_22 (.D(I13), .en(we), .Q(O13), .clk(clk), .clr(reset));
  Register #(.width(32), .Select("low")) register_23 (.D(I21), .en(we), .Q(O21), .clk(clk), .clr(reset));
  Register #(.width(32), .Select("low")) register_24 (.D(I29), .en(we), .Q(O29), .clk(clk), .clr(reset));
  Register #(.width(32), .Select("low")) register_25 (.D(I6), .en(we), .Q(O6), .clk(clk), .clr(reset));
  Register #(.width(32), .Select("low")) register_26 (.D(I14), .en(we), .Q(O14), .clk(clk), .clr(reset));
  Register #(.width(32), .Select("low")) register_27 (.D(I22), .en(we), .Q(O22), .clk(clk), .clr(reset));
  Register #(.width(32), .Select("low")) register_28 (.D(I30), .en(we), .Q(O30), .clk(clk), .clr(reset));
  Register #(.width(32), .Select("low")) register_29 (.D(I7), .en(we), .Q(O7), .clk(clk), .clr(reset));
  Register #(.width(32), .Select("low")) register_30 (.D(I15), .en(we), .Q(O15), .clk(clk), .clr(reset));
  Register #(.width(32), .Select("low")) register_31 (.D(I23), .en(we), .Q(O23), .clk(clk), .clr(reset));
  Register #(.width(32), .Select("low")) register_32 (.D(I31), .en(we), .Q(O31), .clk(clk), .clr(reset));
endmodule

module \右移2位再取低10位  (
  input  [31:0] in_1,
  output [9:0] out_2
);

  wire [31:0] shifter_1_out;

  Shifter #(.width(32), .shift("lr")) shifter_1 (.in(in_1), .\dist (5'b00010), .out(shifter_1_out));
  Bit_Extender #(.in_width(32), .out_width(10), .\type ("zero")) bit_extender_1 (.in(shifter_1_out), .out(out_2));
endmodule

module \寄存器地址生成  (
  input  [1:0] \寄存器写入地址选择 ,
  input  [31:0] \指令 ,
  output [4:0] rs,
  output [4:0] rt,
  output [4:0] \写入地址 
);

  Multiplexer #(.select(2), .width(5), .enable("false")) multiplexer_1 (
    .in0(\指令 [20:16]), .in1(\指令 [15:11]), .in2({5{1'b1}}), .in3({5{1'b1}}), .out(\写入地址 ), .sel(\寄存器写入地址选择 ));

  assign rs = \指令 [25:21];
  assign rt = \指令 [20:16];
endmodule

module \地址计算  (
  input  [31:0] \指令 ,
  input  [31:0] pc,
  output [31:0] \无跳转地址 ,
  output [31:0] \B指令跳转地址 ,
  output [31:0] \J_Jal跳转地址 
);

  wire [31:0] bit_extender_1_out, shifter_1_out;

  assign bit_extender_1_out = {{16{\指令 [15]}}, \指令 [15:0]};  // Bit_Extender bit_extender_1
  Shifter #(.width(32)) shifter_1 (.in(bit_extender_1_out), .\dist (5'b00010), .out(shifter_1_out));
  Adder #(.width(32)) adder_1 (.a(32'h4), .b(pc), .out(\无跳转地址 ));  // open: cin, cout
  Adder #(.width(32)) adder_2 (.a(shifter_1_out), .b(\无跳转地址 ), .out(\B指令跳转地址 ));  // open: cin, cout

  assign \J_Jal跳转地址  = {pc[31:28], \指令 [25:0], 2'b00};

  // Notes on the sheet:
  //   pc+4 + imm16
  //   {pc[31:28], imm26, 2'b00}
endmodule

module \b跳转判断  (
  input  beq,
  input  equal,
  input  bne,
  input  bgez,
  input  [31:0] \寄存器值 ,
  output \b跳转 
);

  wire and_1_out, and_2_out, and_3_out, comparator_1_eq, comparator_1_gt, not_1_out, or_2_out;

  or or_1 (\b跳转 , and_2_out, and_1_out, and_3_out);
  and and_1 (and_1_out, not_1_out, bne);
  and and_2 (and_2_out, beq, equal);
  not not_1 (not_1_out, equal);
  and and_3 (and_3_out, bgez, or_2_out);
  or or_2 (or_2_out, comparator_1_gt, comparator_1_eq);
  Comparator #(.width(32)) comparator_1 (
    .a(\寄存器值 ), .b({32{1'b0}}), .gt(comparator_1_gt), .eq(comparator_1_eq));  // open: lt
endmodule

module \load处理  (
  input  lbu,
  input  \_4字节访存 ,
  input  [31:0] \完整内存地址 ,
  input  [31:0] \内存读出内容 ,
  output [31:0] \访存结果 
);

  wire [7:0] multiplexer_1_out;
  wire [31:0] bit_extender_1_out, bit_extender_2_out, multiplexer_2_out;

  Multiplexer #(.select(2), .width(8), .enable("false")) multiplexer_1 (
    .in0(\内存读出内容 [7:0]), .in1(\内存读出内容 [15:8]), .in2(\内存读出内容 [23:16]), .in3(\内存读出内容 [31:24]),
    .out(multiplexer_1_out), .sel(\完整内存地址 [1:0]));
  assign bit_extender_1_out = {{24{multiplexer_1_out[7]}}, multiplexer_1_out};  // Bit_Extender bit_extender_1
  assign bit_extender_2_out = {{24{1'b0}}, multiplexer_1_out};  // Bit_Extender bit_extender_2
  Multiplexer #(.width(32), .enable("false")) multiplexer_2 (
    .in0(bit_extender_1_out), .in1(bit_extender_2_out), .out(multiplexer_2_out), .sel(lbu));
  Multiplexer #(.width(32), .enable("false")) multiplexer_3 (
    .in0(multiplexer_2_out), .in1(\内存读出内容 ), .out(\访存结果 ), .sel(\_4字节访存 ));
endmodule

module \store处理  (
  input  [31:0] \目前此内存地址的数据 ,
  input  [31:0] \完整内存地址 ,
  input  \_4字节访存 ,
  input  [31:0] \准备写入的数据 ,
  output [31:0] \实际写入的数据 
);

  wire [31:0] multiplexer_1_out;

  Multiplexer #(.select(2), .width(32), .enable("false")) multiplexer_1 (
    .in0({\目前此内存地址的数据 [31:8], \准备写入的数据 [7:0]}),
    .in1({\目前此内存地址的数据 [31:16], \准备写入的数据 [7:0], \目前此内存地址的数据 [7:0]}),
    .in2({\目前此内存地址的数据 [31:24], \准备写入的数据 [7:0], \目前此内存地址的数据 [15:0]}),
    .in3({\准备写入的数据 [7:0], \目前此内存地址的数据 [23:0]}), .out(multiplexer_1_out), .sel(\完整内存地址 [1:0]));
  Pull_Resistor pull_resistor_1 (.node(\实际写入的数据 ));
  Multiplexer #(.width(32), .enable("false")) multiplexer_2 (
    .in0(multiplexer_1_out), .in1(\准备写入的数据 ), .out(\实际写入的数据 ), .sel(\_4字节访存 ));
endmodule

module \立即数处理  (
  input  \符号扩展 ,
  input  [15:0] \_16位立即数 ,
  output [31:0] \_32位立即数 
);

  wire [31:0] bit_extender_1_out, bit_extender_2_out;

  assign bit_extender_1_out = {{16{1'b0}}, \_16位立即数 };  // Bit_Extender bit_extender_1
  assign bit_extender_2_out = {{16{\_16位立即数 [15]}}, \_16位立即数 };  // Bit_Extender bit_extender_2
  Multiplexer #(.width(32), .enable("false")) multiplexer_1 (
    .in0(bit_extender_1_out), .in1(bit_extender_2_out), .out(\_32位立即数 ), .sel(\符号扩展 ));
endmodule

module \hi_lo_寄存器  (
  input  clk,
  input  reset,
  input  we,
  input  [31:0] \HI输入 ,
  input  [31:0] \LO输入 ,
  output [31:0] HI,
  output [31:0] LO
);

  Register #(.width(32), .Select("low")) register_1 (.D(\HI输入 ), .en(we), .Q(HI), .clk(clk), .clr(reset));
  Register #(.width(32), .Select("low")) register_2 (.D(\LO输入 ), .en(we), .Q(LO), .clk(clk), .clr(reset));
  // Probe on HI
  // Probe on LO
endmodule
